// Logisim project cpu.circ as structural Verilog: 1 circuit, main circuit cpu
module cpu (
  input  clk,
  input  [31:0] INSTRUCTION,
  input  [31:0] READ_DATA,
  output [31:0] WRITE_ADDRESS,
  output [31:0] PROGRAM_COUNTER,
  output [31:0] ra,
  output [31:0] sp,
  output [31:0] t0,
  output [31:0] t1,
  output [31:0] t2,
  output [31:0] s0,
  output [31:0] s1,
  output [31:0] a0,
  output [31:0] tohost,
  output [3:0] WRITE_ENABLE,
  output [31:0] WRITE_DATA
);

  wire ASel, BrEq, BrLt, BrUn, BSel, CSRSel, CSRWen, MemRW, PCSel, RegWEn;
  wire [1:0] WBSel;
  wire [2:0] control_logic_1_immsel;
  wire [3:0] ALUSel;
  wire [31:0] adder_1_out, DataA, DataD, imm, multiplexer_1_out, multiplexer_2_out, PCadd4;

  Adder #(.width(32)) adder_1 (.a(PROGRAM_COUNTER), .b(32'h4), .out(adder_1_out));  // open: cin, cout
  Register #(.width(32)) PC (.D(adder_1_out), .clk(clk), .Q(PROGRAM_COUNTER));  // open: en, clr
  control_logic control_logic_1 (
    .CSRWen(CSRWen), .PCSel(PCSel), .RegWEn(RegWEn), .ImmSel(control_logic_1_immsel), .BrUn(BrUn),
    .ASel(ASel), .BSel(BSel), .ALUSel(ALUSel), .MemRW(MemRW), .WBSel(WBSel), .CSRSel(CSRSel),
    .inst(INSTRUCTION), .BrEq(BrEq), .BrLt(BrLt));
  regfile regfile_1 (
    .rs1(INSTRUCTION[19:15]), .rs2(INSTRUCTION[24:20]), .rd(INSTRUCTION[11:7]), .Write_Data(DataD),
    .RegWEn(RegWEn), .clk(clk), .ra(ra), .sp(sp), .t0(t0), .t1(t1), .t2(t2), .s0(s0), .s1(s1), .a0(a0),
    .Read_Data_1(DataA), .Read_Data_2(WRITE_DATA));
  imm_gen imm_gen_1 (.inst(INSTRUCTION), .ImmSel(control_logic_1_immsel), .imm(imm));
  // branch_comp branch_comp_1: pin names not known
  Multiplexer #(.enable("false"), .width(32)) multiplexer_1 (
    .in0(DataA), .out(multiplexer_1_out), .sel(ASel));  // open: in1
  Multiplexer #(.enable("false"), .width(32)) multiplexer_2 (
    .in0(WRITE_DATA), .in1(imm), .out(multiplexer_2_out), .sel(BSel));
  alu alu_1 (.Result(WRITE_ADDRESS), .A(multiplexer_1_out), .B(multiplexer_2_out), .ALUSel(ALUSel));
  csr csr_1 (.tohost(tohost));  // open: CSR_address, CSR_din, CSR_WE, clk
  Multiplexer #(.enable("false"), .select(2), .width(32)) multiplexer_3 (
    .in0(READ_DATA), .in1(WRITE_ADDRESS), .in2(PCadd4), .out(DataD), .sel(WBSel));  // open: in3

  assign WRITE_ENABLE = 4'b0000;

  // Other names for the same wires on the sheet: ALUres[31:0] = WRITE_ADDRESS; DataB[31:0] = WRITE_DATA;
  //   rd[4:0] = INSTRUCTION[11:7]; rs1[4:0] = INSTRUCTION[19:15]; rs2[4:0] = INSTRUCTION[24:20]

  // Notes on the sheet:
  //   Output to IMEM
  //   IMEM (do **NOT** move this)
  //   Inputs from IMEM
  //   It is OK to move the PC, RegFile, ALU, MEM, Branch Comp, Imm Gen, and Control Logic to wherever is most convenient for you when constructing your CPU, and to delete this text
  //   Inputs/Outputs for testing. Do **NOT** move these.
  //   Outputs To DMEM
  //   DMEM (do **NOT** move this)
  //   Inputs From DMEM
endmodule
